# Fritzing sketch meteo_board_schema (saved by Fritzing 0.8.7b)
perfboards: 1
stripboards: 2

parts:
  Componente1 = Arduino Nano (Rev3.0)
  J2 = Screw terminal - 2 pins [package=THT]  # not connected
  J4 = Screw terminal - 2 pins [package=THT]  # not connected
  J5 = Screw terminal - 2 pins [package=THT]  # not connected
  J6 = Screw terminal - 2 pins [package=THT]  # not connected
  J7 = Screw terminal - 2 pins [package=THT]
  J8 = Screw terminal - 2 pins [package=THT]
  J9 = Screw terminal - 2 pins [package=THT]
  J10 = Screw terminal - 2 pins [package=THT]
  J11 = Screw terminal - 2 pins [package=THT]  # not connected
  J12 = Screw terminal - 2 pins [package=THT]
  J13 = Screw terminal - 2 pins [package=THT]
  J14 = Screw terminal - 2 pins [package=THT]  # not connected
  DS1 = DS18B20 1-Wire Temperature Sensor [part_number=DS18B20]  # not connected
  R1 = Resistor [tolerance=±5% resistance=4.7k package=THT]
  APC220 = APC220 with antenna  # not connected
  LCD1 = LCD screen  # not connected
  J17 = female pin header, 7 pins [form="♀ (female)"]
  J18 = Screw terminal - 2 pins [package=THT]  # not connected
  J19 = Screw terminal - 2 pins [package=THT]  # not connected
  J20 = Screw terminal - 2 pins [package=THT]
  R2 = Resistor [tolerance=±5% resistance=10k package=THT]

nets:
  N1: Componente1.D1/TX, J17.pin4
  N2: Componente1.D0/RX, J17.pin3
  N3: Componente1.GND, J8.pin1, J9.pin2, J12.pin1, J17.pin7, R2.Pin_1
  N4: Componente1.D4, J13.pin2
  N5: Componente1.D5, J13.pin1
  N6: Componente1.D6, J10.pin2
  N7: Componente1.D7, J10.pin1
  N8: Componente1.D11/MOSI, J9.pin1
  N9: Componente1.D12/MISO, R1.Pin_1, J20.pin1
  N10: Componente1.5V, J7.pin1, J12.pin2, R1.Pin_0, J17.pin6
  N11: Componente1.A1, J7.pin2, R2.Pin_0

custom parts:
  APC220 with antenna: Radio transceiver module for Arduino operating in the 418-455MHz band.
